# Fritzing sketch perkit_control (saved by Fritzing 0.3.5b)
breadboards: 1

parts:
  Arduino1 = Arduino
  S1 = Pushbutton [package=THT]
  LED1 = Red LED - 5mm
  R2 = 10 Ω Resistor [package=THT]

nets:
  N1: Arduino1.GND, LED1.cathode
  N2: Arduino1.D2, S1.Pin_1, S1.Pin_2, LED1.anode
  N3: Arduino1.+5V, R2.Pin_0
  N4: S1.Pin_3, S1.Pin_4, R2.Pin_1

notes:
  Basic setuo for switching a radio on/off.
